// Logisim project ARM_1.circ as structural Verilog: 25 circuits, main circuit main
module main (
  output [7:0] out_1,
  output [31:0] r0,
  output [31:0] r1,
  output [31:0] r2,
  output [31:0] r3,
  output [31:0] r4,
  output [31:0] r5,
  output [31:0] r6,
  output [31:0] r7,
  output [31:0] r8,
  output [31:0] r9,
  output [31:0] r10,
  output [31:0] r11,
  output [31:0] r12,
  output [31:0] r13,
  output [31:0] r14,
  output [31:0] r15
);

  wire clk, cmp_1_no_rd, imm_or_not, it_is_B, mov_1_move, multiplexer_2_out, N, not_2_out, not_3_out,
       not_4_out, not_5_out, P, S, Z;
  wire [3:0] immediate_or_not_grabber_1_rm, operation;
  wire [4:4] not_1_out;
  wire [31:0] controlled_buffer_1_out, imm, main_registers_1_rm_val, main_registers_1_rn_val,
       multiplexer_1_out, new_PC, Rd, Rm, rom_1_data;
  wire [31:8] shifter_1_out;

  not not_1 (not_1_out[4], 1'b1);
  Shifter #(.shift("lr"), .width(32)) shifter_1 (
    .in(r15), .\dist ({{3{not_1_out[4]}}, 1'b1, not_1_out[4]}), .out({shifter_1_out, out_1}));
  ROM #(.dataWidth(32)) rom_1 (.addr(out_1), .data(rom_1_data));
  Clock u_clk (.out(clk));
  B b_1 (.A(rom_1_data), .pc(r15), .Z(Z), .N(N), .P(P), .it_is_B(it_is_B), .new_pc(new_PC));
  not not_2 (not_2_out, it_is_B);
  assign {controlled_buffer_1_out[31:21], S, controlled_buffer_1_out[19:0]} = not_2_out ? rom_1_data : 32'bz;  // Controlled_Buffer controlled_buffer_1
  CMP cmp_1 (.A(controlled_buffer_1_out[24:21]), .no_Rd(cmp_1_no_rd), .operation(operation));
  immediate_or_not_grabber immediate_or_not_grabber_1 (
    .input_val(rom_1_data), .Rm(immediate_or_not_grabber_1_rm), .imm(imm), .imm_or_not(imm_or_not));
  MOV mov_1 (.operation(operation), .move(mov_1_move));
  Multiplexer #(.width(32)) multiplexer_1 (.in0(Rd), .in1(Rm), .out(multiplexer_1_out), .sel(mov_1_move));
  not not_3 (not_3_out, cmp_1_no_rd);
  not not_4 (not_4_out, it_is_B);
  Multiplexer multiplexer_2 (.in0(not_3_out), .in1(not_4_out), .out(multiplexer_2_out), .sel(it_is_B));
  condition_codes condition_codes_1 (.result(Rd), .S(S), .clk(clk), .N(N), .P(P), .Z(Z));
  main_registers main_registers_1 (
    .Rn(controlled_buffer_1_out[19:16]), .Rm(immediate_or_not_grabber_1_rm),
    .Rd(controlled_buffer_1_out[15:12]), .Rd_val(multiplexer_1_out), .new_pc(new_PC), .we(multiplexer_2_out),
    .clk(clk), .Rn_val(main_registers_1_rn_val), .Rm_val(main_registers_1_rm_val), .r0(r0), .r1(r1), .r2(r2),
    .r3(r3), .r4(r4), .r5(r5), .r6(r6), .r7(r7), .r8(r8), .r9(r9), .r10(r10), .r11(r11), .r12(r12),
    .r13(r13), .r14(r14), .r15(r15));
  not not_5 (not_5_out, imm_or_not);
  Multiplexer #(.width(32)) multiplexer_3 (.in0(imm), .in1(main_registers_1_rm_val), .out(Rm), .sel(not_5_out));
  alu_main alu_main_1 (.operand_0(main_registers_1_rn_val), .operand_1(Rm), .operation(operation), .result(Rd));

  // Other names for the same wires on the sheet: PC[31:0] = r15

  // Notes on the sheet:
  //   contents of rom_1 (hex, n*v repeats v):
  //   e3a0000a e3a01000 e3a02005 ea000002 e0811000 e2422001 e3520000 ea000002
endmodule

module B (
  input  [31:0] A,
  input  [31:0] pc,
  input  Z,
  input  N,
  input  P,
  output it_is_B,
  output [31:0] new_pc
);

  wire code_match_1_t_or_f, neg_offset;
  wire [1:1] not_1_out;
  wire [4:0] not_2_out;
  wire [23:0] shifter_1_out, sign_a_o;
  wire [31:0] adder_1_out, adder_2_out, bit_extender_1_out, bit_extender_2_out, multiplexer_1_out,
       subtractor_1_out;

  and and_1 (it_is_B, A[27], ~A[26], A[25], ~A[24]);  // AND_Gate
  not not_1 (not_1_out[1], 1'b1);
  assign bit_extender_1_out = {{29{1'b0}}, {1'b1, {2{not_1_out[1]}}}};  // Bit_Extender bit_extender_1
  code_match code_match_1 (
    .Z(Z), .N(N), .P(P), .code(A[31:28]), .instruction(A[27:24]), .T_or_F(code_match_1_t_or_f));  // open: beq, bne, bge, blt, bgt, ble, b
  Adder #(.width(32)) adder_1 (.a(pc), .b(bit_extender_1_out), .out(adder_1_out));  // open: cin, cout
  not not_2 (not_2_out[0], 1'b1);
  not not_3 (not_2_out[4], 1'b1);
  Shifter #(.width(24)) shifter_1 (
    .in(sign_a_o), .\dist ({{3{not_2_out[4]}}, 1'b1, not_2_out[0]}), .out(shifter_1_out));
  program_counter program_counter_1 (.offset(A[23:0]), .sign_adjusted_offset(sign_a_o), .neg_or_pos(neg_offset));
  assign bit_extender_2_out = {{8{1'b0}}, shifter_1_out};  // Bit_Extender bit_extender_2
  Adder #(.width(32)) adder_2 (.a(adder_1_out), .b(bit_extender_2_out), .out(adder_2_out));  // open: cin, cout
  Subtractor #(.width(32)) subtractor_1 (
    .a(adder_1_out), .b(bit_extender_2_out), .out(subtractor_1_out));  // open: bin, bout
  Multiplexer #(.width(32)) multiplexer_1 (
    .in0(adder_2_out), .in1(subtractor_1_out), .out(multiplexer_1_out), .sel(neg_offset));
  Multiplexer #(.width(32)) multiplexer_2 (
    .in0(adder_1_out), .in1(multiplexer_1_out), .out(new_pc), .sel(code_match_1_t_or_f));

  // Other names for the same wires on the sheet: offset[23:0] = A[23:0]
endmodule

module program_counter (
  input  [23:0] offset,
  output [23:0] sign_adjusted_offset,
  output neg_or_pos
);

  wire [23:0] adder_1_out, bit_extender_1_out, controlled_inverter_1_out;

  assign controlled_inverter_1_out = offset[23] ? ~offset : 24'bz;  // Controlled_Inverter controlled_inverter_1
  assign bit_extender_1_out = {{23{1'b0}}, 1'b1};  // Bit_Extender bit_extender_1
  Adder #(.width(24)) adder_1 (
    .a(controlled_inverter_1_out), .b(bit_extender_1_out), .out(adder_1_out));  // open: cin, cout
  Multiplexer #(.width(24)) multiplexer_1 (
    .in0(offset), .in1(adder_1_out), .out(sign_adjusted_offset), .sel(offset[23]));

  assign neg_or_pos = offset[23];
endmodule

module immediate_or_not_grabber (
  input  [31:0] input_val,
  output [3:0] Rm,
  output [31:0] imm,
  output imm_or_not
);

  wire not_2_out;
  wire [0:0] not_3_out;
  wire [4:0] rot_x_two;
  wire [4:4] not_1_out;
  wire [31:0] bit_extender_1_out, shifter_2_out;

  not not_1 (not_1_out[4], input_val[25]);
  assign Rm = not_2_out ? input_val[3:0] : 4'bz;  // Controlled_Buffer controlled_buffer_1
  not not_2 (not_2_out, input_val[25]);
  not not_3 (not_3_out[0], not_1_out[4]);
  assign bit_extender_1_out = {{24{1'b0}}, input_val[7:0]};  // Bit_Extender bit_extender_1
  Shifter #(.width(5)) shifter_1 (
    .in({not_1_out[4], input_val[11:8]}), .\dist ({{2{not_1_out[4]}}, not_3_out[0]}), .out(rot_x_two));
  Shifter #(.shift("rr"), .width(32)) shifter_2 (.in(bit_extender_1_out), .\dist (rot_x_two), .out(shifter_2_out));
  assign imm = input_val[25] ? shifter_2_out : 32'bz;  // Controlled_Buffer controlled_buffer_2

  assign imm_or_not = input_val[25];

  // Other names for the same wires on the sheet: rot[3:0] = input_val[11:8]; imm_t = input_val[25]
endmodule

module code_match (
  input  Z,
  input  N,
  input  P,
  input  [3:0] code,
  input  [3:0] instruction,
  output beq,
  output bne,
  output bge,
  output T_or_F,
  output blt,
  output bgt,
  output ble,
  output b
);

  wire and_8_out, controlled_buffer_1_out, not_1_out, or_1_out, or_2_out, or_3_out;

  and and_1 (beq, ~code[3], ~code[2], ~code[1], ~code[0]);  // AND_Gate
  and and_2 (bne, ~code[3], ~code[2], ~code[1], code[0]);  // AND_Gate
  and and_3 (bge, code[3], ~code[2], code[1], ~code[0]);  // AND_Gate
  and and_4 (blt, code[3], ~code[2], code[1], code[0]);  // AND_Gate
  and and_5 (bgt, code[3], code[2], ~code[1], ~code[0]);  // AND_Gate
  and and_6 (ble, code[3], code[2], ~code[1], code[0]);  // AND_Gate
  and and_7 (b, code[3], code[2], code[1], ~code[0]);  // AND_Gate
  or or_1 (or_1_out, N, P);
  or or_2 (or_2_out, Z, P);
  or or_3 (or_3_out, Z, N);
  assign controlled_buffer_1_out = beq ? Z : 1'bz;  // Controlled_Buffer controlled_buffer_1
  assign controlled_buffer_1_out = bne ? or_1_out : 1'bz;  // Controlled_Buffer controlled_buffer_2
  assign controlled_buffer_1_out = bge ? or_2_out : 1'bz;  // Controlled_Buffer controlled_buffer_3
  assign controlled_buffer_1_out = blt ? N : 1'bz;  // Controlled_Buffer controlled_buffer_4
  assign controlled_buffer_1_out = bgt ? P : 1'bz;  // Controlled_Buffer controlled_buffer_5
  assign controlled_buffer_1_out = ble ? or_3_out : 1'bz;  // Controlled_Buffer controlled_buffer_6
  assign controlled_buffer_1_out = b ? b : 1'bz;  // Controlled_Buffer controlled_buffer_7
  not not_1 (not_1_out, 1'b1);
  and and_8 (and_8_out, instruction[3], ~instruction[2], instruction[1], ~instruction[0]);  // AND_Gate
  Multiplexer multiplexer_1 (.in0(not_1_out), .in1(controlled_buffer_1_out), .out(T_or_F), .sel(and_8_out));
endmodule

module CMP (
  input  [3:0] A,
  output no_Rd,
  output [3:0] operation
);

  wire [3:3] not_1_out;

  not not_1 (not_1_out[3], A[3]);
  and and_1 (no_Rd, ~A[0], A[1], ~A[2], A[3]);  // AND_Gate
  Multiplexer #(.width(4)) multiplexer_1 (.in0(A), .in1({not_1_out[3], A[2:0]}), .out(operation), .sel(no_Rd));

  // Other names for the same wires on the sheet: not_reg = no_Rd
endmodule

module condition_codes (
  input  [31:0] result,
  input  S,
  input  clk,
  output N,
  output P,
  output Z
);

  wire and_1_out, and_2_out, and_3_out, and_4_out, and_5_out, and_6_out, and_7_out, and_8_out, and_9_out,
       and_10_out, and_11_out, and_12_out, and_13_out, and_14_out, and_15_out, and_16_out, and_17_out,
       multiplexer_1_out, not_1_out;

  Register #(.width(1)) register_1 (.D(result[31]), .en(S), .clk(clk), .Q(N));  // open: clr
  and and_1 (and_1_out, ~result[31], ~result[30]);  // AND_Gate
  not not_1 (not_1_out, result[31]);
  and and_2 (and_2_out, ~result[29], ~result[28]);  // AND_Gate
  and and_3 (and_3_out, ~result[27], ~result[26]);  // AND_Gate
  Multiplexer multiplexer_1 (.in0(not_1_out), .in1(result[31]), .out(multiplexer_1_out), .sel(and_10_out));
  Register #(.width(1)) register_2 (.D(multiplexer_1_out), .en(S), .clk(clk), .Q(P));  // open: clr
  and and_4 (and_4_out, ~result[25], ~result[24]);  // AND_Gate
  and and_5 (and_5_out, ~result[23], ~result[22]);  // AND_Gate
  and and_6 (and_6_out, ~result[21], ~result[20]);  // AND_Gate
  and and_7 (and_7_out, ~result[19], ~result[18]);  // AND_Gate
  Register #(.width(1)) register_3 (.D(and_10_out), .en(S), .clk(clk), .Q(Z));  // open: clr
  and and_8 (and_8_out, ~result[17], ~result[16]);  // AND_Gate
  and and_9 (and_9_out, ~result[15], ~result[14]);  // AND_Gate
  and and_10 (and_10_out, and_1_out, and_2_out, and_3_out, and_4_out, and_5_out, and_6_out, and_7_out, and_8_out, and_9_out, and_11_out, and_12_out, and_13_out, and_14_out, and_15_out, and_16_out, and_17_out);
  and and_11 (and_11_out, ~result[13], ~result[12]);  // AND_Gate
  and and_12 (and_12_out, ~result[11], ~result[10]);  // AND_Gate
  and and_13 (and_13_out, ~result[9], ~result[8]);  // AND_Gate
  and and_14 (and_14_out, ~result[7], ~result[6]);  // AND_Gate
  and and_15 (and_15_out, ~result[5], ~result[4]);  // AND_Gate
  and and_16 (and_16_out, ~result[3], ~result[2]);  // AND_Gate
  and and_17 (and_17_out, ~result[1], ~result[0]);  // AND_Gate
endmodule

module MOV (
  input  [3:0] operation,
  output move
);

  and and_1 (move, operation[0], ~operation[1], operation[2], operation[3]);  // AND_Gate
endmodule

module alu_main (
  input  [31:0] operand_0,
  input  [31:0] operand_1,
  input  [3:0] operation,
  output [31:0] result
);

  wire [31:0] bitwise_and_1_out_3, bitwise_not_1_result, bitwise_or_1_out_3, bitwise_xor_1_out_3,
       minus_0_1_1_r, minus_1_0_1_r, plus_0_1_1_r;

  bitwise_AND bitwise_and_1 (.operand_0(operand_0), .operand_1(operand_1), .out_3(bitwise_and_1_out_3));
  bitwise_XOR bitwise_xor_1 (.operand_0(operand_0), .operand_1(operand_1), .out_3(bitwise_xor_1_out_3));
  minus_0_1 minus_0_1_1 (.op_0(operand_0), .op_1(operand_1), .r(minus_0_1_1_r));  // open: ovf
  minus_1_0 minus_1_0_1 (.op_1(operand_1), .op_0(operand_0), .r(minus_1_0_1_r));  // open: ovf
  plus_0_1 plus_0_1_1 (.op_0(operand_0), .op_1(operand_1), .r(plus_0_1_1_r));  // open: ovf
  bitwise_OR bitwise_or_1 (.operand_0(operand_0), .operand_1(operand_1), .out_3(bitwise_or_1_out_3));
  bitwise_not bitwise_not_1 (.operand_1(operand_1), .result(bitwise_not_1_result));
  Multiplexer #(.select(4), .width(32)) multiplexer_1 (
    .in0(bitwise_and_1_out_3), .in1(bitwise_xor_1_out_3), .in2(minus_0_1_1_r), .in3(minus_1_0_1_r),
    .in4(plus_0_1_1_r), .in12(bitwise_or_1_out_3), .in13(operand_1), .in15(bitwise_not_1_result),
    .out(result), .sel(operation));  // open: in5, in6, in7, in8, in9, in10, in11, in14
endmodule

module mini_bitwise_not (
  input  [7:0] op_0,
  output [7:0] eight_bit_r
);

  not not_1 (eight_bit_r[7], op_0[7]);
  not not_2 (eight_bit_r[6], op_0[6]);
  not not_3 (eight_bit_r[5], op_0[5]);
  not not_4 (eight_bit_r[4], op_0[4]);
  not not_5 (eight_bit_r[3], op_0[3]);
  not not_6 (eight_bit_r[2], op_0[2]);
  not not_7 (eight_bit_r[1], op_0[1]);
  not not_8 (eight_bit_r[0], op_0[0]);
endmodule

module bitwise_not (
  input  [31:0] operand_1,
  output [31:0] result
);

  mini_bitwise_not mini_bitwise_not_1 (.op_0(operand_1[7:0]), .eight_bit_r(result[7:0]));
  mini_bitwise_not mini_bitwise_not_2 (.op_0(operand_1[15:8]), .eight_bit_r(result[15:8]));
  mini_bitwise_not mini_bitwise_not_3 (.op_0(operand_1[23:16]), .eight_bit_r(result[23:16]));
  mini_bitwise_not mini_bitwise_not_4 (.op_0(operand_1[31:24]), .eight_bit_r(result[31:24]));
endmodule

module mini_bitwise_or (
  input  [7:0] op_0,
  input  [7:0] op_1,
  output [7:0] eight_bit_r
);

  or or_1 (eight_bit_r[7], op_0[7], op_1[7]);
  or or_2 (eight_bit_r[6], op_0[6], op_1[6]);
  or or_3 (eight_bit_r[5], op_0[5], op_1[5]);
  or or_4 (eight_bit_r[4], op_0[4], op_1[4]);
  or or_5 (eight_bit_r[3], op_0[3], op_1[3]);
  or or_6 (eight_bit_r[2], op_0[2], op_1[2]);
  or or_7 (eight_bit_r[1], op_0[1], op_1[1]);
  or or_8 (eight_bit_r[0], op_0[0], op_1[0]);
endmodule

module bitwise_OR (
  input  [31:0] operand_0,
  input  [31:0] operand_1,
  output [31:0] out_3
);

  mini_bitwise_or mini_bitwise_or_1 (.op_0(operand_0[7:0]), .op_1(operand_1[7:0]), .eight_bit_r(out_3[7:0]));
  mini_bitwise_or mini_bitwise_or_2 (.op_0(operand_0[15:8]), .op_1(operand_1[15:8]), .eight_bit_r(out_3[15:8]));
  mini_bitwise_or mini_bitwise_or_3 (.op_0(operand_0[23:16]), .op_1(operand_1[23:16]), .eight_bit_r(out_3[23:16]));
  mini_bitwise_or mini_bitwise_or_4 (.op_0(operand_0[31:24]), .op_1(operand_1[31:24]), .eight_bit_r(out_3[31:24]));
endmodule

module plus_0_1 (
  input  [31:0] op_0,
  input  [31:0] op_1,
  output [31:0] r,
  output ovf
);

  Adder #(.width(32)) adder_1 (.a(op_0), .b(op_1), .out(r), .cout(ovf));  // open: cin
endmodule

module minus_1_0 (
  input  [31:0] op_1,
  input  [31:0] op_0,
  output [31:0] r,
  output ovf
);

  Subtractor #(.width(32)) subtractor_1 (.a(op_1), .b(op_0), .out(r), .bout(ovf));  // open: bin
endmodule

module minus_0_1 (
  input  [31:0] op_0,
  input  [31:0] op_1,
  output [31:0] r,
  output ovf
);

  Subtractor #(.width(32)) subtractor_1 (.a(op_0), .b(op_1), .out(r), .bout(ovf));  // open: bin
endmodule

module mini_bitwise_XOR (
  input  [7:0] op_0,
  input  [7:0] op_1,
  output [7:0] eight_bit_r
);

  xor xor_1 (eight_bit_r[7], op_0[7], op_1[7]);
  xor xor_2 (eight_bit_r[6], op_0[6], op_1[6]);
  xor xor_3 (eight_bit_r[5], op_0[5], op_1[5]);
  xor xor_4 (eight_bit_r[4], op_0[4], op_1[4]);
  xor xor_5 (eight_bit_r[3], op_0[3], op_1[3]);
  xor xor_6 (eight_bit_r[2], op_0[2], op_1[2]);
  xor xor_7 (eight_bit_r[1], op_0[1], op_1[1]);
  xor xor_8 (eight_bit_r[0], op_0[0], op_1[0]);
endmodule

module bitwise_XOR (
  input  [31:0] operand_0,
  input  [31:0] operand_1,
  output [31:0] out_3
);

  mini_bitwise_XOR mini_bitwise_xor_1 (.op_0(operand_0[7:0]), .op_1(operand_1[7:0]), .eight_bit_r(out_3[7:0]));
  mini_bitwise_XOR mini_bitwise_xor_2 (.op_0(operand_0[15:8]), .op_1(operand_1[15:8]), .eight_bit_r(out_3[15:8]));
  mini_bitwise_XOR mini_bitwise_xor_3 (.op_0(operand_0[23:16]), .op_1(operand_1[23:16]), .eight_bit_r(out_3[23:16]));
  mini_bitwise_XOR mini_bitwise_xor_4 (.op_0(operand_0[31:24]), .op_1(operand_1[31:24]), .eight_bit_r(out_3[31:24]));
endmodule

module mini_bitwise_AND (
  input  [7:0] op_0,
  input  [7:0] op_1,
  output [7:0] eight_bit_r
);

  and and_1 (eight_bit_r[7], op_0[7], op_1[7]);
  and and_2 (eight_bit_r[6], op_0[6], op_1[6]);
  and and_3 (eight_bit_r[5], op_0[5], op_1[5]);
  and and_4 (eight_bit_r[4], op_0[4], op_1[4]);
  and and_5 (eight_bit_r[3], op_0[3], op_1[3]);
  and and_6 (eight_bit_r[2], op_0[2], op_1[2]);
  and and_7 (eight_bit_r[1], op_0[1], op_1[1]);
  and and_8 (eight_bit_r[0], op_0[0], op_1[0]);
endmodule

module bitwise_AND (
  input  [31:0] operand_0,
  input  [31:0] operand_1,
  output [31:0] out_3
);

  mini_bitwise_AND mini_bitwise_and_1 (.op_0(operand_0[7:0]), .op_1(operand_1[7:0]), .eight_bit_r(out_3[7:0]));
  mini_bitwise_AND mini_bitwise_and_2 (.op_0(operand_0[15:8]), .op_1(operand_1[15:8]), .eight_bit_r(out_3[15:8]));
  mini_bitwise_AND mini_bitwise_and_3 (.op_0(operand_0[23:16]), .op_1(operand_1[23:16]), .eight_bit_r(out_3[23:16]));
  mini_bitwise_AND mini_bitwise_and_4 (.op_0(operand_0[31:24]), .op_1(operand_1[31:24]), .eight_bit_r(out_3[31:24]));
endmodule

module main_registers (
  input  [3:0] Rn,
  input  [3:0] Rm,
  input  [3:0] Rd,
  input  [31:0] Rd_val,
  input  [31:0] new_pc,
  input  we,
  input  clk,
  output [31:0] Rn_val,
  output [31:0] Rm_val,
  output [31:0] r0,
  output [31:0] r1,
  output [31:0] r2,
  output [31:0] r3,
  output [31:0] r4,
  output [31:0] r5,
  output [31:0] r6,
  output [31:0] r7,
  output [31:0] r8,
  output [31:0] r9,
  output [31:0] r10,
  output [31:0] r11,
  output [31:0] r12,
  output [31:0] r13,
  output [31:0] r14,
  output [31:0] r15
);

  reg_file reg_file_1 (
    .Rn(Rn), .Rm(Rm), .Rd(Rd), .Rd_val(Rd_val), .new_pc(new_pc), .we(we), .clk(clk), .Rn_val(Rn_val),
    .Rm_val(Rm_val), .r0(r0), .r1(r1), .r2(r2), .r3(r3), .r4(r4), .r5(r5), .r6(r6), .r7(r7), .r8(r8),
    .r9(r9), .r10(r10), .r11(r11), .r12(r12), .r13(r13), .r14(r14), .r15(r15));
endmodule

module registers (
  input  we,
  input  [3:0] Rd,
  input  [31:0] Rd_val,
  input  [31:0] new_pc,
  input  clk,
  output [31:0] r0,
  output [31:0] r1,
  output [31:0] r2,
  output [31:0] r3,
  output [31:0] r4,
  output [31:0] r5,
  output [31:0] r6,
  output [31:0] r7,
  output [31:0] r8,
  output [31:0] r9,
  output [31:0] r10,
  output [31:0] r11,
  output [31:0] r12,
  output [31:0] r13,
  output [31:0] r14,
  output [31:0] r15
);

  wire demultiplexer_1_out0, demultiplexer_1_out1, demultiplexer_1_out2, demultiplexer_1_out3,
       demultiplexer_1_out4, demultiplexer_1_out5, demultiplexer_1_out6, demultiplexer_1_out7,
       demultiplexer_1_out8, demultiplexer_1_out9, demultiplexer_1_out10, demultiplexer_1_out11,
       demultiplexer_1_out12, demultiplexer_1_out13, demultiplexer_1_out14;
  wire [31:0] demultiplexer_2_out0, demultiplexer_2_out1, demultiplexer_2_out2, demultiplexer_2_out3,
       demultiplexer_2_out4, demultiplexer_2_out5, demultiplexer_2_out6, demultiplexer_2_out7,
       demultiplexer_2_out8, demultiplexer_2_out9, demultiplexer_2_out10, demultiplexer_2_out11,
       demultiplexer_2_out12, demultiplexer_2_out13, demultiplexer_2_out14;

  Demultiplexer #(.select(4)) demultiplexer_1 (
    .out0(demultiplexer_1_out0), .out1(demultiplexer_1_out1), .out2(demultiplexer_1_out2),
    .out3(demultiplexer_1_out3), .out4(demultiplexer_1_out4), .out5(demultiplexer_1_out5),
    .out6(demultiplexer_1_out6), .out7(demultiplexer_1_out7), .out8(demultiplexer_1_out8),
    .out9(demultiplexer_1_out9), .out10(demultiplexer_1_out10), .out11(demultiplexer_1_out11),
    .out12(demultiplexer_1_out12), .out13(demultiplexer_1_out13), .out14(demultiplexer_1_out14), .in(we),
    .sel(Rd));  // open: out15
  Demultiplexer #(.select(4), .width(32)) demultiplexer_2 (
    .out0(demultiplexer_2_out0), .out1(demultiplexer_2_out1), .out2(demultiplexer_2_out2),
    .out3(demultiplexer_2_out3), .out4(demultiplexer_2_out4), .out5(demultiplexer_2_out5),
    .out6(demultiplexer_2_out6), .out7(demultiplexer_2_out7), .out8(demultiplexer_2_out8),
    .out9(demultiplexer_2_out9), .out10(demultiplexer_2_out10), .out11(demultiplexer_2_out11),
    .out12(demultiplexer_2_out12), .out13(demultiplexer_2_out13), .out14(demultiplexer_2_out14), .in(Rd_val),
    .sel(Rd));  // open: out15
  Register #(.width(32)) register_1 (
    .D(demultiplexer_2_out0), .en(demultiplexer_1_out0), .clk(clk), .Q(r0));  // open: clr
  Register #(.width(32)) register_2 (
    .D(demultiplexer_2_out1), .en(demultiplexer_1_out1), .clk(clk), .Q(r1));  // open: clr
  Register #(.width(32)) register_3 (
    .D(demultiplexer_2_out2), .en(demultiplexer_1_out2), .clk(clk), .Q(r2));  // open: clr
  Register #(.width(32)) register_4 (
    .D(demultiplexer_2_out3), .en(demultiplexer_1_out3), .clk(clk), .Q(r3));  // open: clr
  Register #(.width(32)) register_5 (
    .D(demultiplexer_2_out4), .en(demultiplexer_1_out4), .clk(clk), .Q(r4));  // open: clr
  Register #(.width(32)) register_6 (
    .D(demultiplexer_2_out5), .en(demultiplexer_1_out5), .clk(clk), .Q(r5));  // open: clr
  Register #(.width(32)) register_7 (
    .D(demultiplexer_2_out6), .en(demultiplexer_1_out6), .clk(clk), .Q(r6));  // open: clr
  Register #(.width(32)) register_8 (
    .D(demultiplexer_2_out7), .en(demultiplexer_1_out7), .clk(clk), .Q(r7));  // open: clr
  Register #(.width(32)) register_9 (
    .D(demultiplexer_2_out8), .en(demultiplexer_1_out8), .clk(clk), .Q(r8));  // open: clr
  Register #(.width(32)) register_10 (
    .D(demultiplexer_2_out9), .en(demultiplexer_1_out9), .clk(clk), .Q(r9));  // open: clr
  Register #(.width(32)) register_11 (
    .D(demultiplexer_2_out10), .en(demultiplexer_1_out10), .clk(clk), .Q(r10));  // open: clr
  Register #(.width(32)) register_12 (
    .D(demultiplexer_2_out11), .en(demultiplexer_1_out11), .clk(clk), .Q(r11));  // open: clr
  Register #(.width(32)) register_13 (
    .D(demultiplexer_2_out12), .en(demultiplexer_1_out12), .clk(clk), .Q(r12));  // open: clr
  Register #(.width(32)) register_14 (
    .D(demultiplexer_2_out13), .en(demultiplexer_1_out13), .clk(clk), .Q(r13));  // open: clr
  Register #(.width(32)) register_15 (
    .D(demultiplexer_2_out14), .en(demultiplexer_1_out14), .clk(clk), .Q(r14));  // open: clr
  Register #(.width(32)) register_16 (.D(new_pc), .en(clk), .clk(clk), .Q(r15));  // open: clr
endmodule

module reader1 (
  input  [3:0] Rn,
  input  [31:0] r0,
  input  [31:0] r1,
  input  [31:0] r2,
  input  [31:0] r3,
  input  [31:0] r4,
  input  [31:0] r5,
  input  [31:0] r6,
  input  [31:0] r7,
  input  [31:0] r8,
  input  [31:0] r9,
  input  [31:0] r10,
  input  [31:0] r11,
  input  [31:0] r12,
  input  [31:0] r13,
  input  [31:0] r14,
  input  [31:0] r15,
  output [31:0] Rn_val
);

  Multiplexer #(.select(4), .width(32)) multiplexer_1 (
    .in0(r0), .in1(r1), .in2(r2), .in3(r3), .in4(r4), .in5(r5), .in6(r6), .in7(r7), .in8(r8), .in9(r9),
    .in10(r10), .in11(r11), .in12(r12), .in13(r13), .in14(r14), .in15(r15), .out(Rn_val), .sel(Rn));
endmodule

module reader2 (
  input  [3:0] Rm,
  input  [31:0] r0,
  input  [31:0] r1,
  input  [31:0] r2,
  input  [31:0] r3,
  input  [31:0] r4,
  input  [31:0] r5,
  input  [31:0] r6,
  input  [31:0] r7,
  input  [31:0] r8,
  input  [31:0] r9,
  input  [31:0] r10,
  input  [31:0] r11,
  input  [31:0] r12,
  input  [31:0] r13,
  input  [31:0] r14,
  input  [31:0] r15,
  output [31:0] Rm_val
);

  Multiplexer #(.select(4), .width(32)) multiplexer_1 (
    .in0(r0), .in1(r1), .in2(r2), .in3(r3), .in4(r4), .in5(r5), .in6(r6), .in7(r7), .in8(r8), .in9(r9),
    .in10(r10), .in11(r11), .in12(r12), .in13(r13), .in14(r14), .in15(r15), .out(Rm_val), .sel(Rm));
endmodule

module reg_file (
  input  [3:0] Rn,
  input  [3:0] Rm,
  input  [3:0] Rd,
  input  [31:0] Rd_val,
  input  [31:0] new_pc,
  input  we,
  input  clk,
  output [31:0] Rn_val,
  output [31:0] Rm_val,
  output [31:0] r0,
  output [31:0] r1,
  output [31:0] r2,
  output [31:0] r3,
  output [31:0] r4,
  output [31:0] r5,
  output [31:0] r6,
  output [31:0] r7,
  output [31:0] r8,
  output [31:0] r9,
  output [31:0] r10,
  output [31:0] r11,
  output [31:0] r12,
  output [31:0] r13,
  output [31:0] r14,
  output [31:0] r15
);

  registers registers_1 (
    .we(we), .Rd(Rd), .Rd_val(Rd_val), .new_pc(new_pc), .clk(clk), .r0(r0), .r1(r1), .r2(r2), .r3(r3),
    .r4(r4), .r5(r5), .r6(r6), .r7(r7), .r8(r8), .r9(r9), .r10(r10), .r11(r11), .r12(r12), .r13(r13),
    .r14(r14), .r15(r15));
  reader1 reader1_1 (
    .Rn(Rn), .r0(r0), .r1(r1), .r2(r2), .r3(r3), .r4(r4), .r5(r5), .r6(r6), .r7(r7), .r8(r8), .r9(r9),
    .r10(r10), .r11(r11), .r12(r12), .r13(r13), .r14(r14), .r15(r15), .Rn_val(Rn_val));
  reader2 reader2_1 (
    .Rm(Rm), .r0(r0), .r1(r1), .r2(r2), .r3(r3), .r4(r4), .r5(r5), .r6(r6), .r7(r7), .r8(r8), .r9(r9),
    .r10(r10), .r11(r11), .r12(r12), .r13(r13), .r14(r14), .r15(r15), .Rm_val(Rm_val));
endmodule
