// Logisim project counter.circ as structural Verilog: 1 circuit, main circuit main
module main (
  input  clk,
  input  reset,
  output [3:0] out_3
);

  wire d_ff_1_qn, d_ff_2_qn, d_ff_3_qn, d_ff_4_qn;

  D_Flip_Flop d_ff_1 (.D(d_ff_1_qn), .clk(d_ff_2_qn), .Q(out_3[3]), .Qn(d_ff_1_qn), .reset(reset));  // open: preset
  D_Flip_Flop d_ff_2 (.D(d_ff_2_qn), .clk(d_ff_3_qn), .Q(out_3[2]), .Qn(d_ff_2_qn), .reset(reset));  // open: preset
  D_Flip_Flop d_ff_3 (.D(d_ff_3_qn), .clk(d_ff_4_qn), .Q(out_3[1]), .Qn(d_ff_3_qn), .reset(reset));  // open: preset
  D_Flip_Flop d_ff_4 (.D(d_ff_4_qn), .clk(clk), .Q(out_3[0]), .Qn(d_ff_4_qn), .reset(reset));  // open: preset
endmodule
