// Logisim project memory_4_by_3 .circ as structural Verilog: 1 circuit, main circuit main
module main (
  input  [3:0] data_in,
  input  [1:0] write_addr,
  input  clk,
  input  [1:0] read_addr,
  output [3:0] data_out
);

  wire decoder_1_out0, decoder_1_out1, decoder_1_out2, register_1_q, register_2_q, register_3_q,
       register_4_q, register_5_q, register_6_q, register_7_q, register_8_q, register_9_q, register_10_q,
       register_11_q, register_12_q;

  Decoder #(.select(2)) decoder_1 (
    .out0(decoder_1_out0), .out1(decoder_1_out1), .out2(decoder_1_out2), .sel(write_addr));  // open: out3, en
  Register #(.width(1)) register_1 (.D(data_in[3]), .en(decoder_1_out2), .clk(clk), .Q(register_1_q));  // open: clr
  Register #(.width(1)) register_2 (.D(data_in[3]), .en(decoder_1_out1), .clk(clk), .Q(register_2_q));  // open: clr
  Register #(.width(1)) register_3 (.D(data_in[3]), .en(decoder_1_out0), .clk(clk), .Q(register_3_q));  // open: clr
  Register #(.width(1)) register_4 (.D(data_in[2]), .en(decoder_1_out2), .clk(clk), .Q(register_4_q));  // open: clr
  Register #(.width(1)) register_5 (.D(data_in[2]), .en(decoder_1_out1), .clk(clk), .Q(register_5_q));  // open: clr
  Register #(.width(1)) register_6 (.D(data_in[2]), .en(decoder_1_out0), .clk(clk), .Q(register_6_q));  // open: clr
  Multiplexer #(.select(2)) multiplexer_1 (
    .in0(register_3_q), .in1(register_2_q), .in2(register_1_q), .out(data_out[3]), .sel(read_addr));  // open: in3
  Multiplexer #(.select(2)) multiplexer_2 (
    .in0(register_6_q), .in1(register_5_q), .in2(register_4_q), .out(data_out[2]), .sel(read_addr));  // open: in3
  Register #(.width(1)) register_7 (.D(data_in[1]), .en(decoder_1_out2), .clk(clk), .Q(register_7_q));  // open: clr
  Register #(.width(1)) register_8 (.D(data_in[1]), .en(decoder_1_out1), .clk(clk), .Q(register_8_q));  // open: clr
  Register #(.width(1)) register_9 (.D(data_in[1]), .en(decoder_1_out0), .clk(clk), .Q(register_9_q));  // open: clr
  Multiplexer #(.select(2)) multiplexer_3 (
    .in0(register_9_q), .in1(register_8_q), .in2(register_7_q), .out(data_out[1]), .sel(read_addr));  // open: in3
  Register #(.width(1)) register_10 (.D(data_in[0]), .en(decoder_1_out2), .clk(clk), .Q(register_10_q));  // open: clr
  Register #(.width(1)) register_11 (.D(data_in[0]), .en(decoder_1_out1), .clk(clk), .Q(register_11_q));  // open: clr
  Register #(.width(1)) register_12 (.D(data_in[0]), .en(decoder_1_out0), .clk(clk), .Q(register_12_q));  // open: clr
  Multiplexer #(.select(2)) multiplexer_4 (
    .in0(register_12_q), .in1(register_11_q), .in2(register_10_q), .out(data_out[0]), .sel(read_addr));  // open: in3
endmodule
