// Logisim project ripple_carry_adder.circ as structural Verilog: 5 circuits, main circuit main
module main (
  input  [3:0] A,
  input  sub,
  input  [3:0] B,
  output ovf,
  output [3:0] result
);

  wire adding_1_co, adding_2_co, adding_3_co, and_1_out, eight_1_ovf, xor_2_out;
  wire [3:0] positive_negative_1_out_3;

  eight eight_1 (.A(A), .sub(sub), .B(B), .ovf(eight_1_ovf));
  positive_negative positive_negative_1 (.sub(sub), .B(B), .out_3(positive_negative_1_out_3));
  and and_1 (and_1_out, A[0], positive_negative_1_out_3[0]);
  xor xor_1 (result[0], A[0], positive_negative_1_out_3[0]);
  adding adding_1 (
    .A_input(A[1]), .B_input(positive_negative_1_out_3[1]), .carry_in(and_1_out), .co(adding_1_co),
    .r(result[1]));
  adding adding_2 (
    .A_input(A[2]), .B_input(positive_negative_1_out_3[2]), .carry_in(adding_1_co), .co(adding_2_co),
    .r(result[2]));
  adding adding_3 (
    .A_input(A[3]), .B_input(positive_negative_1_out_3[3]), .carry_in(adding_2_co), .co(adding_3_co),
    .r(result[3]));
  xor xor_2 (xor_2_out, adding_2_co, adding_3_co);
  or or_1 (ovf, eight_1_ovf, xor_2_out);
endmodule

module positive_negative (
  input  sub,
  input  [3:0] B,
  output [3:0] out_3
);

  wire and_1_out, and_2_out, and_3_out, xor_1_out, xor_2_out, xor_3_out, xor_4_out;
  wire [3:0] not_1_out;

  assign not_1_out = ~B;  // NOT_Gate not_1, 4 bits wide
  and and_1 (and_1_out, sub, not_1_out[0]);
  and and_2 (and_2_out, not_1_out[1], and_1_out);
  and and_3 (and_3_out, not_1_out[2], and_2_out);
  xor xor_1 (xor_1_out, sub, not_1_out[0]);
  xor xor_2 (xor_2_out, and_1_out, not_1_out[1]);
  xor xor_3 (xor_3_out, and_2_out, not_1_out[2]);
  xor xor_4 (xor_4_out, and_3_out, not_1_out[3]);
  xnor xnor_1 (out_3[2], sub, xor_3_out);
  xnor xnor_2 (out_3[3], sub, xor_4_out);
  xnor xnor_3 (out_3[0], sub, xor_1_out);
  xnor xnor_4 (out_3[1], sub, xor_2_out);
endmodule

module adding (
  input  A_input,
  input  B_input,
  input  carry_in,
  output co,
  output r
);

  wire and_1_out, and_2_out, and_3_out, and_4_out, or_1_out, xnor_1_out, xor_1_out;

  or or_1 (or_1_out, A_input, B_input, carry_in);
  and and_1 (and_1_out, A_input, B_input, carry_in);
  ExactlyOne xor_1 (.out(xor_1_out), .in0(and_2_out), .in1(and_3_out), .in2(and_4_out));
  and and_2 (and_2_out, A_input, B_input);
  and and_3 (and_3_out, B_input, carry_in);
  and and_4 (and_4_out, carry_in, A_input);
  NotExactlyOne xnor_1 (.out(xnor_1_out), .in0(and_2_out), .in1(and_3_out), .in2(and_4_out));
  and and_5 (r, xnor_1_out, or_1_out);
  or or_2 (co, and_1_out, xor_1_out);
endmodule

module overflow (
  input  sub,
  input  [3:0] in_2,
  input  carry_in_to_last,
  input  carry_out_of_last,
  output ovf
);

  wire and_1_out, and_2_out, and_3_out, and_4_out, not_1_out, not_2_out, not_3_out, xor_1_out;

  not not_1 (not_1_out, in_2[2]);
  not not_2 (not_2_out, in_2[1]);
  not not_3 (not_3_out, in_2[0]);
  and and_1 (and_1_out, in_2[3], not_1_out);
  and and_2 (and_2_out, not_2_out, not_3_out);
  and and_3 (and_3_out, and_1_out, and_2_out);
  and and_4 (and_4_out, and_3_out, sub);
  xor xor_1 (xor_1_out, carry_in_to_last, carry_out_of_last);
  or or_1 (ovf, and_4_out, xor_1_out);
endmodule

module eight (
  input  [3:0] A,
  input  sub,
  input  [3:0] B,
  output ovf
);

  wire and_1_out, and_2_out, and_3_out, and_4_out, and_5_out, and_7_out, nand_1_out;

  and and_1 (and_1_out, B[3], ~B[2]);  // AND_Gate
  and and_2 (and_2_out, ~B[1], ~B[0]);  // AND_Gate
  and and_3 (and_3_out, and_1_out, and_2_out);
  and and_4 (and_4_out, and_3_out, sub);
  and and_5 (and_5_out, ~A[3], ~A[2]);  // AND_Gate
  and and_6 (ovf, and_4_out, nand_1_out);
  and and_7 (and_7_out, ~A[1], ~A[0]);  // AND_Gate
  nand nand_1 (nand_1_out, and_5_out, and_7_out);
endmodule
